// Logisim project circuito-compuertas-burbujas.circ as structural Verilog: 1 circuit, main circuit main
module main (
  input  A,
  input  B,
  output C
);

  wire and_1_out, nand_1_out;

  and and_1 (and_1_out, ~A, B);  // AND_Gate
  nand nand_1 (nand_1_out, A, B);
  nor nor_1 (C, and_1_out, nand_1_out);

  // Notes on the sheet:
  //   Función lógica: C = ¬[(¬A · B) ∨ ¬(A · B)] = A · B
  //   Tabla de verdad
  //   A     B     |     C
  //   0     0     |     0
  //   0     1     |     0
  //   1     0     |     0
  //   1     1     |     1
endmodule
