// Logisim project taller-clase-completo.circ as structural Verilog: 16 circuits, main circuit INDICE_TALLER
module INDICE_TALLER (
);


  // Notes on the sheet:
  //   TALLER DE CLASE - LOGISIM
  //   Proyecto único con 15 ejercicios completamente documentados.
  //   Seleccione un circuito en el árbol de la izquierda para abrirlo.
  //   1. Pasar del circuito al álgebra
  //   A_RON
  //   B_GINEBRA
  //   C_WHISKEY
  //   D_AGUA
  //   E_VODKA
  //   F_TEQUILA
  //   G_BRANDY
  //   H_CACHACA
  //   I_PACHARAN
  //   J_VINO
  //   2. Pasar del álgebra al circuito
  //   K_BENEDETTI
  //   L_MACHADO
  //   M_TAGORE
  //   N_CORTAZAR
  //   O_NERUDA
  //   Convención: + = OR, · = AND, ¬ = NOT, ⊕ = XOR.
  //   Cada pestaña incluye circuito, explicación y función.
  //   También incluye su tabla de verdad exhaustiva.
endmodule

module A_RON (
  input  A,
  input  B,
  output RON
);

  wire not_1_out;

  not not_1 (not_1_out, A);
  and and_1 (RON, not_1_out, B);

  // Notes on the sheet:
  //   Ejercicio a — RON
  //   Función original: RON = ¬A · B
  //   Forma simplificada: RON = ¬A · B
  //   Explicación: Se invierte A y el resultado se combina con B
  //   mediante una AND.
  //   Tabla de verdad
  //   A    B    |    RON
  //   0    0    |    0
  //   0    1    |    1
  //   1    0    |    0
  //   1    1    |    0
endmodule

module B_GINEBRA (
  input  A,
  input  B,
  output GINEBRA
);

  wire not_1_out;

  not not_1 (not_1_out, B);
  or or_1 (GINEBRA, A, not_1_out);

  // Notes on the sheet:
  //   Ejercicio b — GINEBRA
  //   Función original: GINEBRA = A + ¬B
  //   Forma simplificada: GINEBRA = A + ¬B
  //   Explicación: B se invierte y luego se aplica OR entre A y ¬B.
  //   Tabla de verdad
  //   A    B    |    GINEBRA
  //   0    0    |    1
  //   0    1    |    0
  //   1    0    |    1
  //   1    1    |    1
endmodule

module C_WHISKEY (
  input  A,
  input  B,
  output WHISKEY
);

  wire and_1_out, not_1_out;

  not not_1 (not_1_out, A);
  and and_1 (and_1_out, A, B);
  or or_1 (WHISKEY, not_1_out, and_1_out);

  // Notes on the sheet:
  //   Ejercicio c — WHISKEY
  //   Función original: WHISKEY = ¬A + A·B
  //   Forma simplificada: WHISKEY = ¬A + B
  //   Explicación: Una rama produce ¬A; la otra A·B. Ambas se unen con
  //   OR.
  //   Tabla de verdad
  //   A    B    |    WHISKEY
  //   0    0    |    1
  //   0    1    |    1
  //   1    0    |    0
  //   1    1    |    1
endmodule

module D_AGUA (
  input  A,
  input  B,
  output AGUA
);

  wire and_1_out, and_2_out, not_1_out, not_2_out;

  not not_1 (not_1_out, A);
  not not_2 (not_2_out, B);
  and and_1 (and_1_out, A, not_2_out);
  and and_2 (and_2_out, not_1_out, B);
  or or_1 (AGUA, and_1_out, and_2_out);

  // Notes on the sheet:
  //   Ejercicio d — AGUA
  //   Función original: AGUA = A·¬B + ¬A·B
  //   Forma simplificada: AGUA = A ⊕ B
  //   Explicación: Las dos AND detectan entradas distintas; la OR
  //   implementa XOR.
  //   Tabla de verdad
  //   A    B    |    AGUA
  //   0    0    |    0
  //   0    1    |    1
  //   1    0    |    1
  //   1    1    |    0
endmodule

module E_VODKA (
  input  A,
  input  B,
  output VODKA
);

  wire nand_1_out, not_1_out;

  not not_1 (not_1_out, A);
  nand nand_1 (nand_1_out, A, B);
  or or_1 (VODKA, not_1_out, nand_1_out);

  // Notes on the sheet:
  //   Ejercicio e — VODKA
  //   Función original: VODKA = ¬A + ¬(A·B)
  //   Forma simplificada: VODKA = ¬A + ¬B = ¬(A·B)
  //   Explicación: Se hace OR entre ¬A y la salida NAND de A con B.
  //   Tabla de verdad
  //   A    B    |    VODKA
  //   0    0    |    1
  //   0    1    |    1
  //   1    0    |    1
  //   1    1    |    0
endmodule

module F_TEQUILA (
  input  A,
  input  B,
  input  C,
  output TEQUILA
);

  wire nand_1_out, nor_1_out;

  nand nand_1 (nand_1_out, A, B);
  nor nor_1 (nor_1_out, B, C);
  or or_1 (TEQUILA, nand_1_out, nor_1_out);

  // Notes on the sheet:
  //   Ejercicio f — TEQUILA
  //   Función original: TEQUILA = ¬(A·B) + ¬(B+C)
  //   Forma simplificada: TEQUILA = ¬A + ¬B = ¬(A·B)
  //   Explicación: Una NAND procesa A,B; una NOR procesa B,C; sus
  //   salidas van a OR.
  //   Tabla de verdad
  //   A    B    C    |    TEQUILA
  //   0    0    0    |    1
  //   0    0    1    |    1
  //   0    1    0    |    1
  //   0    1    1    |    1
  //   1    0    0    |    1
  //   1    0    1    |    1
  //   1    1    0    |    0
  //   1    1    1    |    0
endmodule

module G_BRANDY (
  input  A,
  input  B,
  input  C,
  output BRANDY
);

  wire nand_1_out, not_1_out;

  not not_1 (not_1_out, A);
  nand nand_1 (nand_1_out, A, C);
  or or_1 (BRANDY, not_1_out, B, nand_1_out);

  // Notes on the sheet:
  //   Ejercicio g — BRANDY
  //   Función original: BRANDY = ¬A + B + ¬(A·C)
  //   Forma simplificada: BRANDY = ¬A + B + ¬C
  //   Explicación: La OR de tres entradas reúne ¬A, B y la NAND de A con
  //   C.
  //   Tabla de verdad
  //   A    B    C    |    BRANDY
  //   0    0    0    |    1
  //   0    0    1    |    1
  //   0    1    0    |    1
  //   0    1    1    |    1
  //   1    0    0    |    1
  //   1    0    1    |    0
  //   1    1    0    |    1
  //   1    1    1    |    1
endmodule

module H_CACHACA (
  input  A,
  input  B,
  input  C,
  output CACHACA
);

  wire xnor_1_p3, xor_1_p3;

  // XOR_Gate xor_1: pin names not known; wires that end beside it: A, B, xor_1_p3
  // XNOR_Gate xnor_1: pin names not known; wires that end beside it: B, C, xnor_1_p3
  or or_1 (CACHACA, xor_1_p3, xnor_1_p3);

  // Notes on the sheet:
  //   Ejercicio h — CACHACA
  //   Función original: CACHACA = (A ⊕ B) + ¬(B ⊕ C)
  //   Forma simplificada: CACHACA = (A ⊕ B) + (B XNOR C)
  //   Explicación: La rama superior es XOR, la inferior XNOR y luego se
  //   aplica OR.
  //   Tabla de verdad
  //   A    B    C    |    CACHACA
  //   0    0    0    |    1
  //   0    0    1    |    0
  //   0    1    0    |    1
  //   0    1    1    |    1
  //   1    0    0    |    1
  //   1    0    1    |    1
  //   1    1    0    |    0
  //   1    1    1    |    1
endmodule

module I_PACHARAN (
  input  A,
  input  B,
  input  C,
  output PACHARAN
);

  wire and_1_out, and_2_out, and_3_out, and_4_out, not_1_out, not_2_out, not_3_out;

  not not_1 (not_1_out, A);
  not not_2 (not_2_out, B);
  not not_3 (not_3_out, C);
  and and_1 (and_1_out, not_1_out, B, C);
  and and_2 (and_2_out, not_2_out, C);
  and and_3 (and_3_out, not_1_out, B, not_3_out);
  and and_4 (and_4_out, A, not_3_out);
  or or_1 (PACHARAN, and_1_out, and_2_out, and_3_out, and_4_out);

  // Notes on the sheet:
  //   Ejercicio i — PACHARAN
  //   Función original: PACHARAN = ¬A·B·C + ¬B·C + ¬A·B·¬C + A·¬C
  //   Forma simplificada: PACHARAN = ¬A·B + ¬B·C + A·¬C
  //   Explicación: Cuatro productos canónicos/parciales se combinan
  //   mediante una OR de cuatro entradas.
  //   Tabla de verdad
  //   A    B    C    |    PACHARAN
  //   0    0    0    |    0
  //   0    0    1    |    1
  //   0    1    0    |    1
  //   0    1    1    |    1
  //   1    0    0    |    1
  //   1    0    1    |    1
  //   1    1    0    |    1
  //   1    1    1    |    0
endmodule

module J_VINO (
  input  A,
  input  B,
  input  C,
  output VINO
);

  wire and_1_out, nor_1_out, not_1_out, not_2_out;

  not not_1 (not_1_out, A);
  not not_2 (not_2_out, B);
  nor nor_1 (nor_1_out, not_1_out, not_2_out);
  and and_1 (and_1_out, B, C);
  // XOR_Gate xor_1: pin names not known; wires that end beside it: nor_1_out, and_1_out, VINO

  // Notes on the sheet:
  //   Ejercicio j — VINO
  //   Función original: VINO = ¬(¬A + ¬B) ⊕ (B·C)
  //   Forma simplificada: VINO = (A·B) ⊕ (B·C)
  //   Explicación: La NOR de ¬A,¬B produce A·B; luego se aplica XOR con
  //   B·C.
  //   Tabla de verdad
  //   A    B    C    |    VINO
  //   0    0    0    |    0
  //   0    0    1    |    0
  //   0    1    0    |    0
  //   0    1    1    |    1
  //   1    0    0    |    0
  //   1    0    1    |    0
  //   1    1    0    |    1
  //   1    1    1    |    0
endmodule

module K_BENEDETTI (
  input  A,
  input  B,
  output BENEDETTI
);

  wire and_1_out, nand_1_out, not_1_out, not_2_out;

  not not_1 (not_1_out, A);
  not not_2 (not_2_out, B);
  nand nand_1 (nand_1_out, A, B);
  and and_1 (and_1_out, not_1_out, not_2_out);
  or or_1 (BENEDETTI, nand_1_out, and_1_out);

  // Notes on the sheet:
  //   Álgebra → circuito — BENEDETTI
  //   Función original: BENEDETTI = ¬(A·B) + ¬A·¬B
  //   Forma simplificada: BENEDETTI = ¬(A·B) = ¬A + ¬B
  //   Explicación: Se implementan una NAND y el producto ¬A·¬B; luego se
  //   unen con OR.
  //   Tabla de verdad
  //   A    B    |    BENEDETTI
  //   0    0    |    1
  //   0    1    |    1
  //   1    0    |    1
  //   1    1    |    0
endmodule

module L_MACHADO (
  input  A,
  input  B,
  input  C,
  output MACHADO
);

  wire nand_1_out, nor_1_out, not_1_out;

  not not_1 (not_1_out, C);
  nand nand_1 (nand_1_out, B, C);
  nor nor_1 (nor_1_out, A, not_1_out);
  or or_1 (MACHADO, nand_1_out, nor_1_out);

  // Notes on the sheet:
  //   Álgebra → circuito — MACHADO
  //   Función original: MACHADO = ¬(B·C) + ¬(A + ¬C)
  //   Forma simplificada: MACHADO = ¬A + ¬B + ¬C = ¬(A·B·C)
  //   Explicación: La primera rama es NAND(B,C); la segunda es
  //   NOR(A,¬C); luego OR.
  //   Tabla de verdad
  //   A    B    C    |    MACHADO
  //   0    0    0    |    1
  //   0    0    1    |    1
  //   0    1    0    |    1
  //   0    1    1    |    1
  //   1    0    0    |    1
  //   1    0    1    |    1
  //   1    1    0    |    1
  //   1    1    1    |    0
endmodule

module M_TAGORE (
  input  A,
  input  B,
  input  C,
  output TAGORE
);

  wire nor_1_out, not_1_out, not_2_out, not_3_out;

  not not_1 (not_1_out, B);
  not not_2 (not_2_out, C);
  nor nor_1 (nor_1_out, A, not_2_out);
  not not_3 (not_3_out, not_2_out);
  or or_1 (TAGORE, nor_1_out, not_1_out, not_3_out);

  // Notes on the sheet:
  //   Álgebra → circuito — TAGORE
  //   Función original: TAGORE = ¬(A + ¬C) + ¬B + ¬¬C
  //   Forma simplificada: TAGORE = ¬B + C
  //   Explicación: Se respetan la NOR de A,¬C, el inversor de B y la
  //   doble inversión de C.
  //   Tabla de verdad
  //   A    B    C    |    TAGORE
  //   0    0    0    |    1
  //   0    0    1    |    1
  //   0    1    0    |    0
  //   0    1    1    |    1
  //   1    0    0    |    1
  //   1    0    1    |    1
  //   1    1    0    |    0
  //   1    1    1    |    1
endmodule

module N_CORTAZAR (
  input  A,
  input  B,
  input  C,
  output CORTAZAR
);

  wire nand_1_out, not_1_out;

  not not_1 (not_1_out, B);
  nand nand_1 (nand_1_out, A, not_1_out);
  nor nor_1 (CORTAZAR, nand_1_out, C);

  // Notes on the sheet:
  //   Álgebra → circuito — CORTAZAR
  //   Función original: CORTAZAR = ¬( ¬(A·¬B) + C )
  //   Forma simplificada: CORTAZAR = A·¬B·¬C
  //   Explicación: Se invierte B, se forma ¬(A·¬B) con NAND y la barra
  //   exterior se implementa con NOR.
  //   Tabla de verdad
  //   A    B    C    |    CORTAZAR
  //   0    0    0    |    0
  //   0    0    1    |    0
  //   0    1    0    |    0
  //   0    1    1    |    0
  //   1    0    0    |    1
  //   1    0    1    |    0
  //   1    1    0    |    0
  //   1    1    1    |    0
endmodule

module O_NERUDA (
  input  A,
  input  B,
  input  C,
  output NERUDA
);

  wire nand_1_out, nor_1_out, not_1_out;

  not not_1 (not_1_out, B);
  nor nor_1 (nor_1_out, A, not_1_out);
  nand nand_1 (nand_1_out, not_1_out, C);
  // XNOR_Gate xnor_1: pin names not known; wires that end beside it: nor_1_out, nand_1_out, NERUDA

  // Notes on the sheet:
  //   Álgebra → circuito — NERUDA
  //   Función original: NERUDA = ¬( ¬(A + ¬B) ⊕ ¬(¬B·C) )
  //   Forma simplificada: NERUDA = ¬A·B + ¬A·C + ¬B·C
  //   Explicación: Las ramas NOR(A,¬B) y NAND(¬B,C) entran a una XNOR,
  //   que representa la barra del XOR.
  //   Tabla de verdad
  //   A    B    C    |    NERUDA
  //   0    0    0    |    0
  //   0    0    1    |    1
  //   0    1    0    |    1
  //   0    1    1    |    1
  //   1    0    0    |    0
  //   1    0    1    |    1
  //   1    1    0    |    0
  //   1    1    1    |    0
endmodule
